// Logisim project Assignment_01.circ as structural Verilog: 1 circuit, main circuit main
module main (
  input  in_1,
  input  in_2,
  input  in_3,
  input  in_4,
  input  in_5,
  input  in_6,
  input  in_7,
  input  in_8
);

  wire and_1_out, and_2_out, and_3_out, and_4_out, and_5_out, and_6_out;
  wire [1:0] j_k_ff_8_q;
  wire [2:0] j_k_ff_6_q;
  wire [3:0] j_k_ff_9_q;

  and and_1 (and_1_out, j_k_ff_6_q[2], j_k_ff_6_q[1]);
  and and_2 (and_2_out, and_6_out, j_k_ff_9_q[2]);
  J_K_Flip_Flop j_k_ff_1 (
    .J(and_2_out), .K(and_2_out), .clk(in_5), .Q(j_k_ff_9_q[3]), .reset(and_3_out));  // open: Qn, preset
  and and_3 (and_3_out, j_k_ff_9_q[3], j_k_ff_9_q[1]);
  J_K_Flip_Flop j_k_ff_2 (
    .J(and_5_out), .K(and_5_out), .clk(in_2), .Q(j_k_ff_6_q[2]), .reset(and_1_out));  // open: Qn, preset
  LED led_1 (.in(j_k_ff_6_q[2]));
  LED led_2 (.in(j_k_ff_9_q[3]));
  and and_4 (and_4_out, j_k_ff_8_q[1], j_k_ff_8_q[0]);
  and and_5 (and_5_out, j_k_ff_6_q[0], j_k_ff_6_q[1]);
  J_K_Flip_Flop j_k_ff_3 (
    .J(and_6_out), .K(and_6_out), .clk(in_5), .Q(j_k_ff_9_q[2]), .reset(and_3_out));  // open: Qn, preset
  J_K_Flip_Flop j_k_ff_4 (
    .J(j_k_ff_8_q[0]), .K(j_k_ff_8_q[0]), .clk(in_7), .Q(j_k_ff_8_q[1]), .reset(and_4_out));  // open: Qn, preset
  J_K_Flip_Flop j_k_ff_5 (
    .J(j_k_ff_6_q[0]), .K(j_k_ff_6_q[0]), .clk(in_2), .Q(j_k_ff_6_q[1]), .reset(and_1_out));  // open: Qn, preset
  LED led_3 (.in(j_k_ff_6_q[1]));
  LED led_4 (.in(j_k_ff_9_q[2]));
  LED led_5 (.in(j_k_ff_8_q[1]));
  J_K_Flip_Flop j_k_ff_6 (.J(in_1), .K(in_1), .clk(in_2), .Q(j_k_ff_6_q[0]), .reset(and_1_out));  // open: Qn, preset
  and and_6 (and_6_out, j_k_ff_9_q[0], j_k_ff_9_q[1]);
  J_K_Flip_Flop j_k_ff_7 (
    .J(j_k_ff_9_q[0]), .K(j_k_ff_9_q[0]), .clk(in_5), .Q(j_k_ff_9_q[1]), .reset(and_3_out));  // open: Qn, preset
  J_K_Flip_Flop j_k_ff_8 (.J(in_6), .K(in_6), .clk(in_7), .Q(j_k_ff_8_q[0]), .reset(and_4_out));  // open: Qn, preset
  LED led_6 (.in(j_k_ff_6_q[0]));
  LED led_7 (.in(j_k_ff_9_q[1]));
  LED led_8 (.in(j_k_ff_8_q[0]));
  J_K_Flip_Flop j_k_ff_9 (.J(in_4), .K(in_4), .clk(in_5), .Q(j_k_ff_9_q[0]), .reset(and_3_out));  // open: Qn, preset
  LED led_9 (.in(j_k_ff_9_q[0]));
  Hex_Digit_Display hex_digit_display_1 (.value({{2{in_8}}, j_k_ff_8_q}));  // open: dp
  Hex_Digit_Display hex_digit_display_2 (.value({in_3, j_k_ff_6_q}));  // open: dp
  Hex_Digit_Display hex_digit_display_3 (.value(j_k_ff_9_q));  // open: dp

  // Notes on the sheet:
  //   8
  //   4
  //   2
  //   1
endmodule
