// Logisim project Assignment_01_Kayes_Ahmed.circ as structural Verilog: 1 circuit, main circuit main
module main (
  input  in_1,
  input  in_2,
  input  in_3,
  input  in_4
);

  wire and_1_out, and_2_out, and_3_out, and_4_out, and_5_out, and_6_out, and_7_out, and_8_out, and_9_out,
       and_10_out, and_11_out, and_12_out, and_13_out, and_14_out, and_15_out, and_16_out, and_17_out,
       and_18_out, and_19_out, clock_1_out, clock_2_out, d_ff_7_q, d_ff_7_qn, j_k_ff_1_q, j_k_ff_2_q,
       j_k_ff_3_q, j_k_ff_4_q, j_k_ff_5_q, j_k_ff_6_q, j_k_ff_7_q, j_k_ff_8_q, j_k_ff_9_q, j_k_ff_10_q,
       j_k_ff_11_q, j_k_ff_12_q, j_k_ff_13_q, j_k_ff_14_q, not_1_out, not_2_out, or_1_out, or_2_out;
  wire [1:0] d_ff_3_q;
  wire [3:0] d_ff_1_q, d_ff_8_q, d_ff_10_q;

  J_K_Flip_Flop j_k_ff_1 (.J(in_1), .K(in_1), .clk(and_19_out), .Q(j_k_ff_1_q));  // open: Qn, preset, reset
  and and_1 (and_1_out, j_k_ff_6_q, j_k_ff_2_q);
  or or_1 (or_1_out, and_1_out, and_7_out);
  and and_2 (and_2_out, j_k_ff_1_q, j_k_ff_2_q);
  J_K_Flip_Flop j_k_ff_2 (
    .J(j_k_ff_1_q), .K(j_k_ff_1_q), .clk(and_19_out), .Q(j_k_ff_2_q), .reset(or_1_out));  // open: Qn, preset
  D_Flip_Flop d_ff_1 (.D(j_k_ff_1_q), .clk(or_2_out), .Q(d_ff_1_q[0]));  // open: Qn, preset, reset
  J_K_Flip_Flop j_k_ff_3 (.J(in_1), .K(in_1), .clk(and_4_out), .Q(j_k_ff_3_q), .reset(and_7_out));  // open: Qn, preset
  J_K_Flip_Flop j_k_ff_4 (
    .J(and_2_out), .K(and_2_out), .clk(and_19_out), .Q(j_k_ff_4_q), .reset(or_1_out));  // open: Qn, preset
  D_Flip_Flop d_ff_2 (.D(j_k_ff_2_q), .clk(or_2_out), .Q(d_ff_1_q[1]));  // open: Qn, preset, reset
  J_K_Flip_Flop j_k_ff_5 (
    .J(j_k_ff_3_q), .K(j_k_ff_3_q), .clk(and_4_out), .Q(j_k_ff_5_q), .reset(and_7_out));  // open: Qn, preset
  D_Flip_Flop d_ff_3 (.D(j_k_ff_3_q), .clk(or_2_out), .Q(d_ff_3_q[0]));  // open: Qn, preset, reset
  and and_3 (and_3_out, j_k_ff_4_q, and_2_out);
  J_K_Flip_Flop j_k_ff_6 (
    .J(and_3_out), .K(and_3_out), .clk(and_19_out), .Q(j_k_ff_6_q), .reset(or_1_out));  // open: Qn, preset
  D_Flip_Flop d_ff_4 (.D(j_k_ff_4_q), .clk(or_2_out), .Q(d_ff_1_q[2]));  // open: Qn, preset, reset
  D_Flip_Flop d_ff_5 (.D(j_k_ff_6_q), .clk(or_2_out), .Q(d_ff_1_q[3]));  // open: Qn, preset, reset
  D_Flip_Flop d_ff_6 (.D(j_k_ff_5_q), .clk(or_2_out), .Q(d_ff_3_q[1]));  // open: Qn, preset, reset
  and and_4 (and_4_out, j_k_ff_2_q, j_k_ff_6_q);
  and and_5 (and_5_out, j_k_ff_1_q, j_k_ff_2_q);
  not not_1 (not_1_out, j_k_ff_5_q);
  and and_6 (and_6_out, j_k_ff_3_q, not_1_out);
  and and_7 (and_7_out, and_5_out, and_6_out);
  and and_8 (and_8_out, and_6_out, j_k_ff_2_q);
  D_Flip_Flop d_ff_7 (.D(and_8_out), .clk(and_8_out), .Q(d_ff_7_q), .Qn(d_ff_7_qn));  // open: preset, reset
  Hex_Digit_Display hex_digit_display_1 (.value({in_4, in_3, d_ff_3_q}));  // open: dp
  Hex_Digit_Display hex_digit_display_2 (.value(d_ff_1_q));  // open: dp
  Hex_Digit_Display hex_digit_display_3 (.value(d_ff_10_q));  // open: dp
  Hex_Digit_Display hex_digit_display_4 (.value(d_ff_8_q));  // open: dp
  LED led_1 (.in(d_ff_7_q));
  LED led_2 (.in(d_ff_7_qn));
  Clock clock_1 (.out(clock_1_out));
  Clock clock_2 (.out(clock_2_out));
  and and_9 (and_9_out, clock_2_out, not_2_out);
  not not_2 (not_2_out, in_2);
  and and_10 (and_10_out, in_2, clock_1_out);
  or or_2 (or_2_out, and_9_out, and_10_out);
  J_K_Flip_Flop j_k_ff_7 (.J(in_1), .K(in_1), .clk(or_2_out), .Q(j_k_ff_7_q), .reset(and_11_out));  // open: Qn, preset
  and and_11 (and_11_out, j_k_ff_13_q, j_k_ff_9_q);
  D_Flip_Flop d_ff_8 (.D(j_k_ff_7_q), .clk(or_2_out), .Q(d_ff_8_q[0]));  // open: Qn, preset, reset
  J_K_Flip_Flop j_k_ff_8 (
    .J(in_1), .K(in_1), .clk(and_18_out), .Q(j_k_ff_8_q), .reset(and_12_out));  // open: Qn, preset
  and and_12 (and_12_out, j_k_ff_12_q, j_k_ff_10_q);
  J_K_Flip_Flop j_k_ff_9 (
    .J(j_k_ff_7_q), .K(j_k_ff_7_q), .clk(or_2_out), .Q(j_k_ff_9_q), .reset(and_11_out));  // open: Qn, preset
  D_Flip_Flop d_ff_9 (.D(j_k_ff_9_q), .clk(or_2_out), .Q(d_ff_8_q[1]));  // open: Qn, preset, reset
  J_K_Flip_Flop j_k_ff_10 (
    .J(j_k_ff_8_q), .K(j_k_ff_8_q), .clk(and_18_out), .Q(j_k_ff_10_q), .reset(and_12_out));  // open: Qn, preset
  D_Flip_Flop d_ff_10 (.D(j_k_ff_8_q), .clk(or_2_out), .Q(d_ff_10_q[0]));  // open: Qn, preset, reset
  D_Flip_Flop d_ff_11 (.D(j_k_ff_11_q), .clk(or_2_out), .Q(d_ff_8_q[2]));  // open: Qn, preset, reset
  and and_13 (and_13_out, j_k_ff_10_q, j_k_ff_8_q);
  and and_14 (and_14_out, j_k_ff_9_q, j_k_ff_7_q);
  J_K_Flip_Flop j_k_ff_11 (
    .J(and_14_out), .K(and_14_out), .clk(or_2_out), .Q(j_k_ff_11_q), .reset(and_11_out));  // open: Qn, preset
  J_K_Flip_Flop j_k_ff_12 (
    .J(and_13_out), .K(and_13_out), .clk(and_18_out), .Q(j_k_ff_12_q), .reset(and_12_out));  // open: Qn, preset
  D_Flip_Flop d_ff_12 (.D(j_k_ff_10_q), .clk(or_2_out), .Q(d_ff_10_q[1]));  // open: Qn, preset, reset
  and and_15 (and_15_out, j_k_ff_11_q, and_14_out);
  J_K_Flip_Flop j_k_ff_13 (
    .J(and_15_out), .K(and_15_out), .clk(or_2_out), .Q(j_k_ff_13_q), .reset(and_11_out));  // open: Qn, preset
  D_Flip_Flop d_ff_13 (.D(j_k_ff_13_q), .clk(or_2_out), .Q(d_ff_8_q[3]));  // open: Qn, preset, reset
  and and_16 (and_16_out, j_k_ff_12_q, and_13_out);
  J_K_Flip_Flop j_k_ff_14 (
    .J(and_16_out), .K(and_16_out), .clk(and_18_out), .Q(j_k_ff_14_q), .reset(and_12_out));  // open: Qn, preset
  D_Flip_Flop d_ff_14 (.D(j_k_ff_12_q), .clk(or_2_out), .Q(d_ff_10_q[2]));  // open: Qn, preset, reset
  D_Flip_Flop d_ff_15 (.D(j_k_ff_14_q), .clk(or_2_out), .Q(d_ff_10_q[3]));  // open: Qn, preset, reset
  and and_17 (and_17_out, j_k_ff_8_q, j_k_ff_12_q);
  and and_18 (and_18_out, j_k_ff_13_q, j_k_ff_9_q);
  and and_19 (and_19_out, and_18_out, and_17_out);

  // Notes on the sheet:
  //   Alarm Clock
  //   PM
  //   AM
endmodule
