// Logisim project ANDNOTGATE.circ as structural Verilog: 1 circuit, main circuit main
module main (
  input  Pin_1,
  input  Pin_2,
  input  Pin_1_2
);

  wire and_1_out, not_1_out;

  and and_1 (and_1_out, Pin_1, Pin_2);
  not not_1 (not_1_out, Pin_1_2);
  LED led_1 (.in(and_1_out));
  LED led_2 (.in(not_1_out));

  // Notes on the sheet:
  //   NOT Gate
  //   AND Gate
  //   SAAD IBN JAMIL  STUDENT ID: 103837887
endmodule
