// Logisim project FULLADDER.circ as structural Verilog: 1 circuit, main circuit main
module main (
  input  A,
  input  B,
  input  Ci
);

  wire and_1_out, and_2_out, or_1_out, xor_1_out, xor_2_out;

  and and_1 (and_1_out, A, B);
  xor xor_1 (xor_1_out, A, B);
  xor xor_2 (xor_2_out, xor_1_out, Ci);
  and and_2 (and_2_out, xor_1_out, Ci);
  LED led_1 (.in(xor_2_out));
  or or_1 (or_1_out, and_1_out, and_2_out);
  LED led_2 (.in(or_1_out));

  // Notes on the sheet:
  //   FULL ADDER
  //   A XOR B
  //   A.B
  //   Ci(A XOR B)
  //   SUM
  //   KAYES AHMED KOUSHIK
  //   CARRY
endmodule
