// Logisim project HALFADDER.circ as structural Verilog: 1 circuit, main circuit main
module main (
  input  in_1,
  input  in_2,
  input  in_3,
  input  in_4,
  input  in_5,
  input  in_6,
  input  in_7,
  input  in_8
);

  wire and_1_out, and_2_out, and_3_out, and_4_out, and_5_out, xor_1_out, xor_2_out, xor_3_out, xor_4_out;

  and and_1 (and_1_out, in_2, in_1);
  xor xor_1 (xor_1_out, in_1, in_2);
  xor xor_2 (xor_2_out, in_3, in_4);
  and and_2 (and_2_out, in_4, in_3);
  xor xor_3 (xor_3_out, in_5, in_6);
  and and_3 (and_3_out, in_6, in_5);
  xor xor_4 (xor_4_out, in_7, in_8);
  and and_4 (and_4_out, in_8, in_7);
  LED led_1 (.in(xor_3_out));
  LED led_2 (.in(and_3_out));
  LED led_3 (.in(xor_4_out));
  LED led_4 (.in(and_4_out));
  // XOR_Gate xor_5 has open pins: in0=xor_2_out, in1=and_1_out, out=open
  and and_5 (and_5_out, xor_2_out, and_1_out);
  LED led_5 (.in(xor_1_out));
  LED led_6 (.in(and_1_out));
  // OR_Gate or_1 has open pins: in0=and_5_out, in1=and_2_out, out=open
endmodule
