// Logisim project D_FLIP_FLOP.circ as structural Verilog: 1 circuit, main circuit main
module main (
  input  in_1,
  input  in_2
);

  wire and_1_out, and_2_out, clock_1_out, d_ff_1_q, nor_1_out, nor_2_out, not_1_out;

  Clock clock_1 (.out(clock_1_out));
  not not_1 (not_1_out, in_2);
  D_Flip_Flop d_ff_1 (.D(clock_1_out), .clk(in_1), .Q(d_ff_1_q));  // open: Qn, preset, reset
  and and_1 (and_1_out, clock_1_out, not_1_out);
  and and_2 (and_2_out, clock_1_out, in_2);
  LED led_1 (.in(d_ff_1_q));
  nor nor_1 (nor_1_out, and_1_out, nor_2_out);
  nor nor_2 (nor_2_out, nor_1_out, and_2_out);
  LED led_2 (.in(nor_1_out));
  LED led_3 (.in(nor_2_out));

  // Notes on the sheet:
  //   Clock
  //   Data
  //   Q
  //   Q'
  //   D FLIP FLOP
endmodule
