// Logisim project RS_FLIP_FLOP_OPERATIONS.circ as structural Verilog: 1 circuit, main circuit main
module main (
  input  _1,
  input  in_2,
  input  Set,
  input  in_4
);

  wire nand_1_out, nand_2_out, nand_3_out, nand_4_out;

  nand nand_1 (nand_1_out, _1, nand_2_out);
  nand nand_2 (nand_2_out, nand_1_out, in_2);
  LED led_1 (.in(nand_1_out));
  LED led_2 (.in(nand_2_out));
  nand nand_3 (nand_3_out, Set, nand_4_out);
  nand nand_4 (nand_4_out, nand_3_out, in_4);
  LED led_3 (.in(nand_3_out));
  LED led_4 (.in(nand_4_out));

  // Notes on the sheet:
  //   Set 
  //   Reset
  //   1
  //   RS Flip Flop Operations
  //   Q =1
  //   Q' =0
  //   Reset
  //   Set State
  //   1
  //   1
  //   Q =1
  //   Q' =0
  //   Reset State
endmodule
