// Logisim project R_SFlipFlop.circ as structural Verilog: 1 circuit, main circuit main
module main (
  input  in_1,
  input  Reset
);

  wire nor_1_out, nor_2_out;

  nor nor_1 (nor_1_out, in_1, nor_2_out);
  nor nor_2 (nor_2_out, nor_1_out, Reset);
  LED led_1 (.in(nor_1_out));
  LED led_2 (.in(nor_2_out));

  // Notes on the sheet:
  //   Set
  //   R_S Flip Flop
endmodule
