// Logisim project 8_Bit_Register.circ as structural Verilog: 1 circuit, main circuit main
module main (
  input  in_1,
  input  in_2,
  input  in_3,
  input  in_4,
  input  in_5,
  input  in_6,
  input  in_7,
  input  in_8
);

  wire clock_1_out, d_ff_1_q, d_ff_2_q, d_ff_3_q, d_ff_4_q, d_ff_5_q, d_ff_6_q, d_ff_7_q, d_ff_8_q;

  Clock clock_1 (.out(clock_1_out));
  D_Flip_Flop d_ff_1 (.D(in_1), .clk(clock_1_out), .Q(d_ff_1_q));  // open: Qn, preset, reset
  D_Flip_Flop d_ff_2 (.D(in_2), .clk(clock_1_out), .Q(d_ff_2_q));  // open: Qn, preset, reset
  LED led_1 (.in(d_ff_1_q));
  LED led_2 (.in(d_ff_2_q));
  D_Flip_Flop d_ff_3 (.D(in_3), .clk(clock_1_out), .Q(d_ff_3_q));  // open: Qn, preset, reset
  D_Flip_Flop d_ff_4 (.D(in_4), .clk(clock_1_out), .Q(d_ff_4_q));  // open: Qn, preset, reset
  LED led_3 (.in(d_ff_3_q));
  D_Flip_Flop d_ff_5 (.D(in_5), .clk(clock_1_out), .Q(d_ff_5_q));  // open: Qn, preset, reset
  LED led_4 (.in(d_ff_4_q));
  D_Flip_Flop d_ff_6 (.D(in_6), .clk(clock_1_out), .Q(d_ff_6_q));  // open: Qn, preset, reset
  LED led_5 (.in(d_ff_5_q));
  D_Flip_Flop d_ff_7 (.D(in_7), .clk(clock_1_out), .Q(d_ff_7_q));  // open: Qn, preset, reset
  LED led_6 (.in(d_ff_6_q));
  LED led_7 (.in(d_ff_7_q));
  D_Flip_Flop d_ff_8 (.D(in_8), .clk(clock_1_out), .Q(d_ff_8_q));  // open: Qn, preset, reset
  LED led_8 (.in(d_ff_8_q));

  // Notes on the sheet:
  //   Clock
  //   data
  //   128
  //   64
  //   8 Bit Register
  //   32
  //   16
  //   8
  //   4
  //   2
  //   1
endmodule
