// Logisim project Jai_Cornes_Recording_07.circ as structural Verilog: 1 circuit, main circuit main
module main (
  input  in_1,
  input  in_2,
  input  in_3,
  input  in_4,
  input  in_5,
  input  in_6
);

  wire and_1_out, and_2_out, clock_1_out, clock_2_out, j_k_ff_1_q, j_k_ff_3_q, j_k_ff_4_q, j_k_ff_6_q,
       j_k_ff_8_q;
  wire [2:0] j_k_ff_2_q;

  J_K_Flip_Flop j_k_ff_1 (.J(in_1), .K(in_1), .clk(j_k_ff_3_q), .Q(j_k_ff_1_q));  // open: Qn, preset, reset
  J_K_Flip_Flop j_k_ff_2 (.J(in_5), .K(in_5), .clk(clock_1_out), .Q(j_k_ff_2_q[0]));  // open: Qn, preset, reset
  Clock clock_1 (.out(clock_1_out));
  J_K_Flip_Flop j_k_ff_3 (.J(in_2), .K(in_2), .clk(j_k_ff_4_q), .Q(j_k_ff_3_q));  // open: Qn, preset, reset
  LED led_1 (.in(j_k_ff_2_q[0]));
  J_K_Flip_Flop j_k_ff_4 (.J(in_3), .K(in_3), .clk(j_k_ff_6_q), .Q(j_k_ff_4_q));  // open: Qn, preset, reset
  J_K_Flip_Flop j_k_ff_5 (
    .J(j_k_ff_2_q[0]), .K(j_k_ff_2_q[0]), .clk(clock_1_out), .Q(j_k_ff_2_q[1]));  // open: Qn, preset, reset
  LED led_2 (.in(j_k_ff_2_q[1]));
  J_K_Flip_Flop j_k_ff_6 (.J(in_4), .K(in_4), .clk(clock_2_out), .Q(j_k_ff_6_q));  // open: Qn, preset, reset
  Clock clock_2 (.out(clock_2_out));
  and and_1 (and_1_out, j_k_ff_2_q[0], j_k_ff_2_q[1]);
  J_K_Flip_Flop j_k_ff_7 (
    .J(and_1_out), .K(and_1_out), .clk(clock_1_out), .Q(j_k_ff_2_q[2]));  // open: Qn, preset, reset
  LED led_3 (.in(j_k_ff_2_q[2]));
  and and_2 (and_2_out, and_1_out, j_k_ff_2_q[2]);
  J_K_Flip_Flop j_k_ff_8 (.J(and_2_out), .K(and_2_out), .clk(clock_1_out), .Q(j_k_ff_8_q));  // open: Qn, preset, reset
  LED led_4 (.in(j_k_ff_8_q));
  Hex_Digit_Display hex_digit_display_1 (.value({in_6, j_k_ff_2_q}));  // open: dp

  // Notes on the sheet:
  //   Jai Cornes Recording --7
endmodule
