// Logisim project commonclockcounter 0-5 with buffer.circ as structural Verilog: 1 circuit, main circuit main
module main (
  input  INPUT
);

  wire and_1_out, and_2_out, clock_1_out, d_ff_2_q, d_ff_3_q, j_k_ff_1_q, j_k_ff_2_q, j_k_ff_3_q;

  and and_1 (and_1_out, j_k_ff_2_q, j_k_ff_1_q);
  J_K_Flip_Flop j_k_ff_1 (
    .J(and_2_out), .K(and_2_out), .clk(clock_1_out), .Q(j_k_ff_1_q), .reset(and_1_out));  // open: Qn, preset
  and and_2 (and_2_out, j_k_ff_2_q, j_k_ff_3_q);
  LED led_1 (.in(j_k_ff_1_q));
  J_K_Flip_Flop j_k_ff_2 (
    .J(j_k_ff_3_q), .K(j_k_ff_3_q), .clk(clock_1_out), .Q(j_k_ff_2_q), .reset(and_1_out));  // open: Qn, preset
  D_Flip_Flop d_ff_1 (.D(j_k_ff_1_q), .clk(clock_1_out));  // open: Q, Qn, preset, reset
  D_Flip_Flop d_ff_2 (.D(j_k_ff_2_q), .clk(clock_1_out), .Q(d_ff_2_q));  // open: Qn, preset, reset
  J_K_Flip_Flop j_k_ff_3 (
    .J(INPUT), .K(INPUT), .clk(clock_1_out), .Q(j_k_ff_3_q), .reset(and_1_out));  // open: Qn, preset
  D_Flip_Flop d_ff_3 (.D(j_k_ff_3_q), .clk(clock_1_out), .Q(d_ff_3_q));  // open: Qn, preset, reset
  LED led_2 (.in(d_ff_2_q));
  Clock clock_1 (.out(clock_1_out));
  LED led_3 (.in(d_ff_3_q));

  // Notes on the sheet:
  //   Common Clock COUNTER
  //   CLOCK
endmodule
