// Logisim project commonclockcounter16156.circ as structural Verilog: 1 circuit, main circuit main
module main (
  input  INPUT
);

  wire and_1_out, clock_1_out, j_k_ff_1_q, j_k_ff_2_q, j_k_ff_3_q;

  and and_1 (and_1_out, j_k_ff_2_q, j_k_ff_3_q);
  J_K_Flip_Flop j_k_ff_1 (.J(and_1_out), .K(and_1_out), .clk(clock_1_out), .Q(j_k_ff_1_q));  // open: Qn, preset, reset
  LED led_1 (.in(j_k_ff_1_q));
  J_K_Flip_Flop j_k_ff_2 (
    .J(j_k_ff_3_q), .K(j_k_ff_3_q), .clk(clock_1_out), .Q(j_k_ff_2_q));  // open: Qn, preset, reset
  LED led_2 (.in(j_k_ff_2_q));
  J_K_Flip_Flop j_k_ff_3 (.J(INPUT), .K(INPUT), .clk(clock_1_out), .Q(j_k_ff_3_q));  // open: Qn, preset, reset
  LED led_3 (.in(j_k_ff_3_q));
  Clock clock_1 (.out(clock_1_out));

  // Notes on the sheet:
  //   Common Clock COUNTER
  //   Output 4
  //   output 2
  //   Output 1
  //   CLOCK
endmodule
