// Logisim project Week_3_All_Circuit.circ as structural Verilog: 1 circuit, main circuit main
module main (
  input  in_1,
  input  in_2,
  input  in_3,
  input  in_4,
  input  in_5,
  input  in_6,
  input  in_7,
  input  in_8,
  input  in_9,
  input  in_10,
  input  in_11,
  input  in_12,
  input  in_13,
  input  in_14,
  input  in_15,
  input  in_16,
  input  in_17,
  input  in_18,
  input  Serial_In,
  input  in_20,
  input  in_21,
  input  in_22,
  input  in_23,
  input  in_24
);

  wire and_1_out, and_2_out, and_3_out, and_4_out, clock_1_out, clock_2_out, clock_3_out, clock_4_out,
       clock_5_out, clock_6_out, clock_7_out, clock_8_out, clock_9_out, d_ff_1_q, d_ff_2_q, d_ff_3_q,
       d_ff_4_q, d_ff_5_q, d_ff_6_q, d_ff_7_q, d_ff_8_q, d_ff_10_q, d_ff_11_q, d_ff_12_q, d_ff_13_q,
       d_ff_15_q, d_ff_16_q, d_ff_18_q, d_ff_19_q, d_ff_20_q, d_ff_21_q, d_ff_22_q, d_ff_23_q, j_k_ff_1_q,
       j_k_ff_4_q, j_k_ff_7_q, j_k_ff_9_q, j_k_ff_11_q, j_k_ff_15_q, or_1_out, or_2_out, or_3_out, or_4_out;
  wire [2:0] d_ff_9_q, j_k_ff_2_q, j_k_ff_6_q, j_k_ff_13_q;

  Clock clock_1 (.out(clock_1_out));
  D_Flip_Flop d_ff_1 (.D(in_1), .clk(clock_1_out), .Q(d_ff_1_q));  // open: Qn, preset, reset
  LED led_1 (.in(d_ff_1_q));
  D_Flip_Flop d_ff_2 (.D(in_2), .clk(clock_1_out), .Q(d_ff_2_q));  // open: Qn, preset, reset
  LED led_2 (.in(d_ff_2_q));
  Clock clock_2 (.out(clock_2_out));
  D_Flip_Flop d_ff_3 (.D(in_3), .clk(clock_1_out), .Q(d_ff_3_q));  // open: Qn, preset, reset
  J_K_Flip_Flop j_k_ff_1 (.J(in_9), .K(in_9), .clk(clock_2_out), .Q(j_k_ff_1_q));  // open: Qn, preset, reset
  Clock clock_3 (.out(clock_3_out));
  LED led_3 (.in(d_ff_3_q));
  LED led_4 (.in(j_k_ff_1_q));
  J_K_Flip_Flop j_k_ff_2 (.J(in_10), .K(in_10), .clk(clock_3_out), .Q(j_k_ff_2_q[0]));  // open: Qn, preset, reset
  D_Flip_Flop d_ff_4 (.D(in_4), .clk(clock_1_out), .Q(d_ff_4_q));  // open: Qn, preset, reset
  LED led_5 (.in(d_ff_4_q));
  LED led_6 (.in(j_k_ff_2_q[0]));
  J_K_Flip_Flop j_k_ff_3 (.J(in_12), .K(in_12), .clk(j_k_ff_13_q[1]), .Q(j_k_ff_13_q[2]));  // open: Qn, preset, reset
  Clock clock_4 (.out(clock_4_out));
  Clock clock_5 (.out(clock_5_out));
  Clock clock_6 (.out(clock_6_out));
  D_Flip_Flop d_ff_5 (.D(in_5), .clk(clock_1_out), .Q(d_ff_5_q));  // open: Qn, preset, reset
  J_K_Flip_Flop j_k_ff_4 (.J(in_9), .K(in_9), .clk(j_k_ff_1_q), .Q(j_k_ff_4_q));  // open: Qn, preset, reset
  J_K_Flip_Flop j_k_ff_5 (.J(in_10), .K(in_10), .clk(j_k_ff_2_q[0]), .Q(j_k_ff_2_q[1]));  // open: Qn, preset, reset
  LED led_7 (.in(j_k_ff_13_q[2]));
  J_K_Flip_Flop j_k_ff_6 (
    .J(in_14), .K(in_14), .clk(clock_4_out), .Q(j_k_ff_6_q[0]), .reset(and_3_out));  // open: Qn, preset
  J_K_Flip_Flop j_k_ff_7 (
    .J(in_16), .K(in_16), .clk(clock_5_out), .Q(j_k_ff_7_q), .reset(and_4_out));  // open: Qn, preset
  D_Flip_Flop d_ff_6 (.D(in_18), .clk(clock_6_out), .Q(d_ff_6_q));  // open: Qn, preset, reset
  D_Flip_Flop d_ff_7 (.D(d_ff_13_q), .clk(clock_9_out), .Q(d_ff_7_q));  // open: Qn, preset, reset
  or or_1 (or_1_out, in_24, in_23);
  Clock clock_7 (.out(clock_7_out));
  D_Flip_Flop d_ff_8 (.D(in_6), .clk(clock_1_out), .Q(d_ff_8_q));  // open: Qn, preset, reset
  LED led_8 (.in(d_ff_5_q));
  LED led_9 (.in(j_k_ff_4_q));
  J_K_Flip_Flop j_k_ff_8 (.J(in_12), .K(in_12), .clk(j_k_ff_13_q[0]), .Q(j_k_ff_13_q[1]));  // open: Qn, preset, reset
  LED led_10 (.in(j_k_ff_6_q[0]));
  LED led_11 (.in(j_k_ff_7_q));
  D_Flip_Flop d_ff_9 (.D(j_k_ff_7_q), .clk(clock_5_out), .Q(d_ff_9_q[0]));  // open: Qn, preset, reset
  LED led_12 (.in(d_ff_7_q));
  D_Flip_Flop d_ff_10 (.D(or_1_out), .clk(clock_7_out), .Q(d_ff_10_q));  // open: Qn, preset, reset
  D_Flip_Flop d_ff_11 (.D(in_7), .clk(clock_1_out), .Q(d_ff_11_q));  // open: Qn, preset, reset
  LED led_13 (.in(d_ff_8_q));
  J_K_Flip_Flop j_k_ff_9 (.J(in_9), .K(in_9), .clk(j_k_ff_4_q), .Q(j_k_ff_9_q));  // open: Qn, preset, reset
  LED led_14 (.in(j_k_ff_2_q[1]));
  LED led_15 (.in(j_k_ff_13_q[1]));
  J_K_Flip_Flop j_k_ff_10 (
    .J(j_k_ff_6_q[0]), .K(j_k_ff_6_q[0]), .clk(clock_4_out), .Q(j_k_ff_6_q[1]), .reset(and_3_out));  // open: Qn, preset
  J_K_Flip_Flop j_k_ff_11 (
    .J(j_k_ff_7_q), .K(j_k_ff_7_q), .clk(clock_5_out), .Q(j_k_ff_11_q), .reset(and_4_out));  // open: Qn, preset
  D_Flip_Flop d_ff_12 (.D(d_ff_6_q), .clk(clock_6_out), .Q(d_ff_12_q));  // open: Qn, preset, reset
  LED led_16 (.in(d_ff_6_q));
  D_Flip_Flop d_ff_13 (.D(d_ff_19_q), .clk(clock_9_out), .Q(d_ff_13_q));  // open: Qn, preset, reset
  or or_2 (or_2_out, d_ff_10_q, in_20);
  LED led_17 (.in(d_ff_10_q));
  LED led_18 (.in(d_ff_11_q));
  LED led_19 (.in(j_k_ff_9_q));
  J_K_Flip_Flop j_k_ff_12 (.J(in_10), .K(in_10), .clk(j_k_ff_2_q[1]), .Q(j_k_ff_2_q[2]));  // open: Qn, preset, reset
  Clock clock_8 (.out(clock_8_out));
  LED led_20 (.in(j_k_ff_6_q[1]));
  LED led_21 (.in(j_k_ff_11_q));
  D_Flip_Flop d_ff_14 (.D(j_k_ff_11_q), .clk(clock_5_out), .Q(d_ff_9_q[1]));  // open: Qn, preset, reset
  LED led_22 (.in(d_ff_13_q));
  D_Flip_Flop d_ff_15 (.D(or_2_out), .clk(clock_7_out), .Q(d_ff_15_q));  // open: Qn, preset, reset
  D_Flip_Flop d_ff_16 (.D(in_8), .clk(clock_1_out), .Q(d_ff_16_q));  // open: Qn, preset, reset
  LED led_23 (.in(j_k_ff_2_q[2]));
  J_K_Flip_Flop j_k_ff_13 (.J(in_12), .K(in_12), .clk(clock_8_out), .Q(j_k_ff_13_q[0]));  // open: Qn, preset, reset
  and and_1 (and_1_out, j_k_ff_6_q[0], j_k_ff_6_q[1]);
  J_K_Flip_Flop j_k_ff_14 (
    .J(and_1_out), .K(and_1_out), .clk(clock_4_out), .Q(j_k_ff_6_q[2]), .reset(and_3_out));  // open: Qn, preset
  and and_2 (and_2_out, j_k_ff_7_q, j_k_ff_11_q);
  J_K_Flip_Flop j_k_ff_15 (
    .J(and_2_out), .K(and_2_out), .clk(clock_5_out), .Q(j_k_ff_15_q), .reset(and_4_out));  // open: Qn, preset
  D_Flip_Flop d_ff_17 (.D(j_k_ff_15_q), .clk(clock_5_out), .Q(d_ff_9_q[2]));  // open: Qn, preset, reset
  D_Flip_Flop d_ff_18 (.D(d_ff_12_q), .clk(clock_6_out), .Q(d_ff_18_q));  // open: Qn, preset, reset
  LED led_24 (.in(d_ff_12_q));
  D_Flip_Flop d_ff_19 (.D(d_ff_22_q), .clk(clock_9_out), .Q(d_ff_19_q));  // open: Qn, preset, reset
  or or_3 (or_3_out, d_ff_15_q, in_21);
  LED led_25 (.in(d_ff_15_q));
  LED led_26 (.in(d_ff_16_q));
  LED led_27 (.in(j_k_ff_13_q[0]));
  LED led_28 (.in(j_k_ff_6_q[2]));
  LED led_29 (.in(j_k_ff_15_q));
  LED led_30 (.in(d_ff_18_q));
  LED led_31 (.in(d_ff_19_q));
  D_Flip_Flop d_ff_20 (.D(or_3_out), .clk(clock_7_out), .Q(d_ff_20_q));  // open: Qn, preset, reset
  Hex_Digit_Display hex_digit_display_1 (.value({in_11, j_k_ff_2_q}));  // open: dp
  and and_3 (and_3_out, j_k_ff_6_q[1], j_k_ff_6_q[2]);
  and and_4 (and_4_out, j_k_ff_11_q, j_k_ff_15_q);
  D_Flip_Flop d_ff_21 (.D(d_ff_18_q), .clk(clock_6_out), .Q(d_ff_21_q));  // open: Qn, preset, reset
  LED led_32 (.in(d_ff_22_q));
  D_Flip_Flop d_ff_22 (.D(Serial_In), .clk(clock_9_out), .Q(d_ff_22_q));  // open: Qn, preset, reset
  or or_4 (or_4_out, d_ff_20_q, in_22);
  LED led_33 (.in(d_ff_20_q));
  Hex_Digit_Display hex_digit_display_2 (.value({in_13, j_k_ff_13_q}));  // open: dp
  Clock clock_9 (.out(clock_9_out));
  D_Flip_Flop d_ff_23 (.D(or_4_out), .clk(clock_7_out), .Q(d_ff_23_q));  // open: Qn, preset, reset
  Hex_Digit_Display hex_digit_display_3 (.value({in_15, j_k_ff_6_q}));  // open: dp
  LED led_34 (.in(d_ff_21_q));
  LED led_35 (.in(d_ff_23_q));
  LED led_36 (.in(d_ff_23_q));
  Hex_Digit_Display hex_digit_display_4 (.value({in_17, d_ff_9_q}));  // open: dp

  // Notes on the sheet:
  //   The Asynchronous (Ripple) counter
  //   Serial In
  //   Shift Register
  //   Serial To Parallal Conversion
  //   3 Bit Common Clock - Little Endian - No illegal state
  //   Serial out
  //   3 Bit Common Clock - Little Endian
  //   Left To Right
  //   Right to Left
  //   Serial Out
endmodule
