// Logisim project Common_JK_Buffer.circ as structural Verilog: 1 circuit, main circuit main
module main (
  input  in_1
);

  wire and_1_out, clock_1_out, j_k_ff_1_q, j_k_ff_1_qn, j_k_ff_2_q, j_k_ff_3_q, not_1_out;
  wire [2:0] d_ff_1_q;

  Clock clock_1 (.out(clock_1_out));
  not not_1 (not_1_out, j_k_ff_1_qn);
  J_K_Flip_Flop j_k_ff_1 (
    .J(j_k_ff_1_qn), .K(not_1_out), .clk(clock_1_out), .Q(j_k_ff_1_q), .Qn(j_k_ff_1_qn), .reset(j_k_ff_3_q));  // open: preset
  LED led_1 (.in(j_k_ff_1_q));
  D_Flip_Flop d_ff_1 (.D(j_k_ff_1_q), .clk(clock_1_out), .Q(d_ff_1_q[0]));  // open: Qn, preset, reset
  J_K_Flip_Flop j_k_ff_2 (
    .J(j_k_ff_1_q), .K(j_k_ff_1_q), .clk(clock_1_out), .Q(j_k_ff_2_q), .reset(j_k_ff_3_q));  // open: Qn, preset
  LED led_2 (.in(j_k_ff_2_q));
  D_Flip_Flop d_ff_2 (.D(j_k_ff_2_q), .clk(clock_1_out), .Q(d_ff_1_q[1]));  // open: Qn, preset, reset
  and and_1 (and_1_out, j_k_ff_1_q, j_k_ff_2_q);
  J_K_Flip_Flop j_k_ff_3 (
    .J(and_1_out), .K(and_1_out), .clk(clock_1_out), .Q(j_k_ff_3_q), .reset(j_k_ff_3_q));  // open: Qn, preset
  LED led_3 (.in(j_k_ff_3_q));
  D_Flip_Flop d_ff_3 (.D(j_k_ff_3_q), .clk(clock_1_out), .Q(d_ff_1_q[2]));  // open: Qn, preset, reset
  // AND_Gate and_2 has open pins: in0=j_k_ff_2_q, in1=j_k_ff_3_q, out=open
  Hex_Digit_Display hex_digit_display_1 (.value({in_1, d_ff_1_q}));  // open: dp

  // Notes on the sheet:
  //   Jai Cornes Recording 08 
endmodule
